# Fritzing sketch Schema (saved by Fritzing 0.9.2b)
breadboards: 1

parts:
  S1 = Pushbutton [package="[THT]"]
  S2 = Pushbutton [package="[THT]"]
  S3 = Pushbutton [package="[THT]"]
  S4 = Pushbutton [package="[THT]"]
  R1 = Resistor [tolerance=±5% resistance=220 package=THT]
  R2 = Resistor [tolerance=±5% resistance=220 package=THT]
  R3 = Resistor [tolerance=±5% resistance=220 package=THT]
  R4 = Resistor [tolerance=±5% resistance=220 package=THT]
  Part1 = Intel Edison Arduinobreakout
  LED1 = LED - 5mm [color="Red (633nm)" package="5 mm [THT]"]
  LED2 = LED - 5mm [color="Red (633nm)" package="5 mm [THT]"]
  LED3 = LED - 5mm [color="Red (633nm)" package="5 mm [THT]"]
  LED4 = LED - 5mm [color="Red (633nm)" package="5 mm [THT]"]
  LED5 = LED - 5mm [color="Red (633nm)" package="5 mm [THT]"]
  LED6 = LED - 5mm [color="Red (633nm)" package="5 mm [THT]"]
  LED7 = LED - 5mm [color="Red (633nm)" package="5 mm [THT]"]
  LED8 = LED - 5mm [color="Red (633nm)" package="5 mm [THT]"]
  LED9 = LED - 5mm [color="Red (633nm)" package="5 mm [THT]"]
  LED10 = LED - 5mm [color="Red (633nm)" package="5 mm [THT]"]
  LED11 = LED - 5mm [color="Red (633nm)" package="5 mm [THT]"]
  LED12 = LED - 5mm [color="Red (633nm)" package="5 mm [THT]"]
  R5 = Resistor [tolerance=±5% resistance=220 package=THT]
  R6 = Resistor [tolerance=±5% resistance=220 package=THT]
  R7 = Resistor [tolerance=±5% resistance=220 package=THT]
  R8 = Resistor [tolerance=±5% resistance=220 package=THT]
  R9 = Resistor [tolerance=±5% resistance=220 package=THT]
  R10 = Resistor [tolerance=±5% resistance=220 package=THT]
  R11 = Resistor [tolerance=±5% resistance=220 package=THT]
  R12 = Resistor [tolerance=±5% resistance=220 package=THT]
  R13 = Resistor [tolerance=±5% resistance=220 package=THT]
  R14 = Resistor [tolerance=±5% resistance=220 package=THT]
  R15 = Resistor [tolerance=±5% resistance=220 package=THT]
  R17 = Resistor [tolerance=±5% resistance=220 package=THT]
  U1 = 74HC595 [package="DIP16 [THT]"]
  U2 = 74HC595 [package="DIP16 [THT]"]

nets:
  N1: S1.Pin_1, S1.Pin_2, R4.Pin_1, Part1.D11_PWM/MOSI
  VCC: S1.Pin_3, S1.Pin_4, S2.Pin_3, S2.Pin_4, S3.Pin_3, S3.Pin_4, S4.Pin_3, S4.Pin_4, Part1.5V, U1.MR, U1.VCC, U2.MR, U2.VCC
  N2: S2.Pin_1, S2.Pin_2, R3.Pin_1, Part1.D10_PWM/SS
  N3: S3.Pin_1, S3.Pin_2, R2.Pin_1, Part1.D9_PWM
  N4: S4.Pin_1, S4.Pin_2, R1.Pin_1, Part1.D8
  GND: R1.Pin_0, R2.Pin_0, R3.Pin_0, R4.Pin_0, Part1.GND, R5.Pin_1, R6.Pin_1, R7.Pin_1, R8.Pin_1, R9.Pin_1, R10.Pin_1, R11.Pin_0, R12.Pin_0, R13.Pin_0, R14.Pin_0, R15.Pin_0, U1.GND, U1.OE, U2.GND, U2.OE
  N5: Part1.D0/RX, U1.DS
  N6: Part1.D1/TX, U1.ST_CP, U2.ST_CP
  N7: Part1.D2, U1.SH_CP, U2.SH_CP
  N8: LED1.cathode, R17.Pin_1
  N9: LED1.anode, U1.Q0
  N10: LED2.cathode, R15.Pin_1
  N11: LED2.anode, U1.Q1
  N12: LED3.cathode, R14.Pin_1
  N13: LED3.anode, U1.Q2
  N14: LED4.cathode, R13.Pin_1
  N15: LED4.anode, U1.Q3
  N16: LED5.cathode, R12.Pin_1
  N17: LED5.anode, U1.Q4
  N18: LED6.cathode, R11.Pin_1
  N19: LED6.anode, U1.Q5
  N20: LED7.cathode, R10.Pin_0
  N21: LED7.anode, U2.Q0
  N22: LED8.cathode, R9.Pin_0
  N23: LED8.anode, U2.Q1
  N24: LED9.cathode, R8.Pin_0
  N25: LED9.anode, U2.Q2
  N26: LED10.cathode, R7.Pin_0
  N27: LED10.anode, U2.Q3
  N28: LED11.cathode, R6.Pin_0
  N29: LED11.anode, U2.Q4
  N30: LED12.cathode, R5.Pin_0
  N31: LED12.anode, U2.Q5
  N32: U1.Q7', U2.DS
